# Fritzing sketch autogrow (saved by Fritzing 0.9.3b)
breadboards: 1

parts:
  Part1 = Arduino Mega 2560 (Rev3)
  Part2 = Real Time Clock Module - DS1307 RTC Breakout Board
  DS1 = DS18B20 1-Wire Temperature Sensor [part_number=DS18B20]
  R1 = Resistor [tolerance=±5% resistance=4.7k package="2512 [SMD]"]
  U1 = LCD-16X2 [package=lcd-16x2]
  R3 = Trimmer Potentiometer [maximum_resistance=10kΩ package=THT]
  R4 = Resistor [tolerance=±5% resistance=1k package="2512 [SMD]"]
  U3 = RELAY [package=relay-jzc]  # not connected
  U4 = RELAY [package=relay-jzc]  # not connected
  U5 = RELAY [package=relay-jzc]  # not connected
  U6 = RELAY [package=relay-jzc]  # not connected
  U7 = RELAY [package=relay-jzc]  # not connected
  U8 = RELAY [package=relay-jzc]  # not connected
  U9 = RELAY [package=relay-jzc]

nets:
  N1: Part1.D21/SCL, Part2.SCL
  N2: Part1.D20/SDA, Part2.SDA
  5V: Part1.5V, Part2.5V, DS1.VDD, R1.Pin_0, U1.VDD, R3.leg2, R4.Pin_0, U9.NO
  GND: Part1.GND, Part2.GND, DS1.GND, U1.VSS, U1.K, R3.leg1, U9.NC
  N3: Part1.D22, DS1.DQ, R1.Pin_1
  N4: Part1.D24, U1.DB6
  N5: Part1.D25, U1.DB7
  N6: Part1.D26, U1.DB4
  N7: Part1.D27, U1.DB5
  N8: Part1.D28, U1.RS
  N9: Part1.D29, U1.E
  N10: U1.VO, R3.wiper
  N11: U1.A, R4.Pin_1
